// Digital circuit LAB1_CS303.dig as structural Verilog
module LAB1_CS303 (
  input  x3,
  input  x2,
  input  x1,
  input  x0,
  output out
);

  wire and_1_out, and_2_out, and_3_out, and_4_out, not_1_out, not_2_out, not_3_out;

  not not_1 (not_1_out, x3);
  not not_2 (not_2_out, x2);
  not not_3 (not_3_out, x1);
  and and_1 (and_1_out, not_1_out, not_2_out, x1);
  and and_2 (and_2_out, not_1_out, x2, x0);
  and and_3 (and_3_out, x2, not_3_out, x0);
  and and_4 (and_4_out, not_2_out, x1, x0);
  or or_1 (out, and_1_out, and_2_out, and_3_out, and_4_out);
endmodule
